# Fritzing sketch Diagram (saved by Fritzing 0.9.3b)
breadboards: 1

parts:
  Arduino_Mega = Arduino Mega ADK (Rev3)
  RTC_Module = Real Time Clock Module - DS1307 RTC Breakout Board
  M1 = ph-4502c [package=THT]
  SD_card_module1 = SD Card Module
  DS1 = DS18B20 1-Wire Temperature Sensor [part_number=DS18B20]
  R1 = Resistor [tolerance=±5% resistance=1k package="2010 [SMD]"]

nets:
  N1: Arduino_Mega.A0, M1.pin3
  N2: Arduino_Mega.A1, M1.pin1
  N3: Arduino_Mega.D21/SCL, RTC_Module.SCL
  N4: Arduino_Mega.D20/SDA, RTC_Module.SDA
  5V: Arduino_Mega.IOREF, Arduino_Mega.5V, RTC_Module.5V, M1.pin6, SD_card_module1.+5, DS1.VDD, R1.Pin_0
  GND: Arduino_Mega.GND, RTC_Module.GND, M1.pin4, M1.pin5, SD_card_module1.GND#0, DS1.GND
  N5: Arduino_Mega.D22, DS1.DQ, R1.Pin_1
  N6: Arduino_Mega.D50/MISO, SD_card_module1.MISO
  N7: Arduino_Mega.D51/MOSI, SD_card_module1.MOSI
  N8: Arduino_Mega.D52/SCK, SD_card_module1.SCK
  N9: Arduino_Mega.D53/SS, SD_card_module1.CS

notes:
  DS18B20
  SD card module
  pH sensor bridge

custom parts:
  ph-4502c: ph-4502c PH Meter.
  SD Card Module: SD Card Module Slot Socket Reader For Arduino ARM MCU
